# Fritzing sketch Node (saved by Fritzing 0.9.3b)
circuit board: 7.15039cm x 5.60221cm
breadboards: 1

parts:
  R1 = Resistor [tolerance=±5% resistance=4.7k package=THT]
  U1 = NodeMCU V1.0
  S1 = Pushbutton [package="[THT]"]
  LED1 = LED - 5mm [color="Red (633nm)" package="5 mm [THT]"]
  Part1 = 16 NeoPixel Ring [part_number=1463]

nets:
  N1: R1.Pin_0, U1.D2, S1.Pin_3, S1.Pin_4
  GND: R1.Pin_1, U1.GND, LED1.anode, Part1.GND
  N2: U1.D0, LED1.cathode
  N3: U1.D1, Part1.IN
  3V3: U1.3V3, S1.Pin_1, S1.Pin_2, Part1.VDD

custom parts:
  NodeMCU V1.0: ESP8266 based NodeMCU
  16 NeoPixel Ring: 16 ultra bright smart LED NeoPixels are arranged in a circle with 1.75" (44.5mm) outer diameter. The rings are 'chainable' - connect the output pin of one to the input pin of another. Use only one microcontroller pin to control as many as you can chain together! Each LED is addressable as the driver chip is inside the LED. Each one has ~18mA constant current drive so the color will be very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
